// Logisim project ISA.circ as structural Verilog: 4 circuits, main circuit my circuit
module my_circuit (
  input  in_1,
  input  in_2,
  input  in_3,
  input  in_4,
  input  in_5,
  input  in_6,
  input  in_7
);

  wire [31:0] adder_1_out, IR_q, PC_q, undriven;

  Adder #(.width(32)) adder_1 (.a(PC_q), .b(32'h4), .out(adder_1_out));  // open: cin, cout
  Register #(.width(32)) PC (.D(adder_1_out), .en(in_1), .Q(PC_q), .clk(in_2), .clr(in_3));
  Register #(.width(32)) IR (.D(undriven), .en(in_6), .Q(IR_q), .clk(in_2));  // open: clr

  // Other names for the same wires on the sheet: BYTE = in_7; CK = in_2; CLR_PC = in_3; LD_IR = in_6; LD_MAR = in_4;
  //   LD_MDR = in_5; LD_PC = in_1
endmodule

module memory (
  input  [31:0] MDR_IN,
  input  [31:0] MAR_IN,
  input  LD_MAR,
  input  LD_MDR,
  input  in_5,
  input  in_6,
  input  in_7,
  output [31:0] MDR_OUT
);

  wire [1:0] BYTE;
  wire [5:0] CRAP;
  wire [7:0] multiplexer_1_out, ram_1_data, ram_2_data, ram_3_data, ram_4_data;
  wire [25:2] MAR_q;
  wire [31:0] bit_extender_1_out, MDR_IN_t, multiplexer_2_out;

  Register #(.width(32)) MAR (.D(MAR_IN), .en(LD_MAR), .Q({CRAP, MAR_q, BYTE}), .clk(in_5));  // open: clr
  RAM #(.addrWidth(24)) ram_1 (.addr(MAR_q), .data(ram_1_data), .clk(in_5), .ld(in_6));  // open: sel, clr
  RAM #(.addrWidth(24)) ram_2 (.addr(MAR_q), .data(ram_2_data), .clk(in_5), .ld(in_6));  // open: sel, clr
  RAM #(.addrWidth(24)) ram_3 (.addr(MAR_q), .data(ram_3_data), .clk(in_5), .ld(in_6));  // open: sel, clr
  RAM #(.addrWidth(24)) ram_4 (.addr(MAR_q), .data(ram_4_data), .clk(in_5), .ld(in_6));  // open: sel, clr
  Multiplexer #(.select(2), .width(8), .disabled(0), .enable("false")) multiplexer_1 (
    .in0(ram_1_data), .in1(ram_2_data), .in2(ram_3_data), .in3(ram_4_data), .out(multiplexer_1_out),
    .sel(BYTE));
  Demultiplexer #(.width(32), .disabled(0), .enable("false")) demultiplexer_1 (
    .out0({ram_4_data, ram_3_data, ram_2_data, ram_1_data}), .out1(MDR_IN_t), .in(MDR_IN), .sel(in_7));
  assign bit_extender_1_out = {{24{1'b0}}, multiplexer_1_out};  // Bit_Extender bit_extender_1
  Multiplexer #(.width(32), .disabled(0), .enable("false")) multiplexer_2 (
    .in0({ram_4_data, ram_3_data, ram_2_data, ram_1_data}), .in1(bit_extender_1_out),
    .out(multiplexer_2_out), .sel(in_7));
  Register #(.width(32)) MDR (.D(multiplexer_2_out), .en(LD_MDR), .Q(MDR_OUT), .clk(in_5));  // open: clr

  // Other names for the same wires on the sheet: CK = in_5; L = in_6; SIZE = in_7
endmodule

module register_file (
  input  [3:0] DST_REG,
  input  [31:0] DATA_IN,
  input  [3:0] REG_A,
  input  [3:0] REG_B,
  input  CK,
  input  WE,
  output [31:0] OUT_A,
  output [31:0] OUT_B
);

  wire demultiplexer_1_out0, demultiplexer_1_out1, demultiplexer_1_out2, demultiplexer_1_out3;
  wire [31:0] register_group_1_out_a, register_group_1_out_b, register_group_2_out_a, register_group_2_out_b,
       register_group_3_out_a, register_group_3_out_b, register_group_4_out_a, register_group_4_out_b;

  Demultiplexer #(.select(2), .disabled(0), .enable("false")) demultiplexer_1 (
    .out0(demultiplexer_1_out0), .out1(demultiplexer_1_out1), .out2(demultiplexer_1_out2),
    .out3(demultiplexer_1_out3), .in(WE), .sel(DST_REG[3:2]));
  register_group register_group_1 (
    .REG_A(REG_A[1:0]), .REG_B(REG_B[1:0]), .DATA_IN(DATA_IN), .DST_REG(DST_REG[1:0]),
    .WE(demultiplexer_1_out0), .CK(CK), .OUT_A(register_group_1_out_a), .OUT_B(register_group_1_out_b));
  register_group register_group_2 (
    .REG_A(REG_A[1:0]), .REG_B(REG_B[1:0]), .DATA_IN(DATA_IN), .DST_REG(DST_REG[1:0]),
    .WE(demultiplexer_1_out1), .CK(CK), .OUT_A(register_group_2_out_a), .OUT_B(register_group_2_out_b));
  register_group register_group_3 (
    .REG_A(REG_A[1:0]), .REG_B(REG_B[1:0]), .DATA_IN(DATA_IN), .DST_REG(DST_REG[1:0]),
    .WE(demultiplexer_1_out2), .CK(CK), .OUT_A(register_group_3_out_a), .OUT_B(register_group_3_out_b));
  register_group register_group_4 (
    .REG_A(REG_A[1:0]), .REG_B(REG_B[1:0]), .DATA_IN(DATA_IN), .DST_REG(DST_REG[1:0]),
    .WE(demultiplexer_1_out3), .CK(CK), .OUT_A(register_group_4_out_a), .OUT_B(register_group_4_out_b));
  Multiplexer #(.select(2), .width(32), .disabled(0), .enable("false")) multiplexer_1 (
    .in0(register_group_1_out_a), .in1(register_group_2_out_a), .in2(register_group_3_out_a),
    .in3(register_group_4_out_a), .out(OUT_A), .sel(REG_A[3:2]));
  Multiplexer #(.select(2), .width(32), .disabled(0), .enable("false")) multiplexer_2 (
    .in0(register_group_1_out_b), .in1(register_group_2_out_b), .in2(register_group_3_out_b),
    .in3(register_group_4_out_b), .out(OUT_B), .sel(REG_B[3:2]));

  // Other names for the same wires on the sheet: D_REG[1:0] = DST_REG[1:0]; D_GRP[1:0] = DST_REG[3:2];
  //   A_REG[1:0] = REG_A[1:0]; A_GRP[1:0] = REG_A[3:2]; B_REG[1:0] = REG_B[1:0]; B_GRP[1:0] = REG_B[3:2]
endmodule

module register_group (
  input  [31:0] DATA_IN,
  input  [1:0] DST_REG,
  input  [1:0] REG_A,
  input  [1:0] REG_B,
  input  WE,
  input  CK,
  output [31:0] OUT_A,
  output [31:0] OUT_B
);

  wire demultiplexer_1_out0, demultiplexer_1_out1, demultiplexer_1_out2, demultiplexer_1_out3;
  wire [31:0] register_1_q, register_2_q, register_3_q, register_4_q;

  Demultiplexer #(.select(2), .disabled(0), .enable("false")) demultiplexer_1 (
    .out0(demultiplexer_1_out0), .out1(demultiplexer_1_out1), .out2(demultiplexer_1_out2),
    .out3(demultiplexer_1_out3), .in(WE), .sel(DST_REG));
  Register #(.width(32)) register_1 (.D(DATA_IN), .en(demultiplexer_1_out0), .Q(register_1_q), .clk(CK));  // open: clr
  Register #(.width(32)) register_2 (.D(DATA_IN), .en(demultiplexer_1_out1), .Q(register_2_q), .clk(CK));  // open: clr
  Register #(.width(32)) register_3 (.D(DATA_IN), .en(demultiplexer_1_out2), .Q(register_3_q), .clk(CK));  // open: clr
  Register #(.width(32)) register_4 (.D(DATA_IN), .en(demultiplexer_1_out3), .Q(register_4_q), .clk(CK));  // open: clr
  Multiplexer #(.select(2), .width(32), .disabled(0), .enable("false")) multiplexer_1 (
    .in0(register_1_q), .in1(register_2_q), .in2(register_3_q), .in3(register_4_q), .out(OUT_A), .sel(REG_A));
  Multiplexer #(.select(2), .width(32), .disabled(0), .enable("false")) multiplexer_2 (
    .in0(register_1_q), .in1(register_2_q), .in2(register_3_q), .in3(register_4_q), .out(OUT_B), .sel(REG_B));
endmodule
