// Logisim project PipelinedLC2200.circ as structural Verilog: 11 circuits, main circuit my circuit
module my_circuit (
  input  in_1,
  input  in_2,
  input  in_3
);

  wire CK, LD_REG;
  wire [3:0] dbuf_1_reg_dst_out, ebuf_1_reg_dst_out, fbuf_1_reg_dst_out, fbuf_1_reg_sr1_out,
       fbuf_1_reg_sr2_out, REG_DST;
  wire [7:0] dbuf_1_opcode_out, ebuf_1_opcode_out, fbuf_1_opcode_out, mbuf_1_opcode_out;
  wire [15:0] fbuf_1_immediate_val_out;
  wire [31:0] alu_1_b_out, alu_1_out, bit_extender_1_out, d_mem_1_data_out, dbuf_1_imm_out, dbuf_1_pc_out,
       dbuf_1_sr1_out, dbuf_1_sr2_out, DST_VAL, ebuf_1_alu_val_out, ebuf_1_word_val_out, fbuf_1_pc_out,
       i_mem_1_data_out, multiplexer_1_out, PC, PC_q, register_file_1_out_a, register_file_1_out_b, undriven;

  Clock CLOCK (.out(CK));
  Adder #(.width(32)) adder_1 (.a(PC_q), .b(32'h1), .out(PC));  // open: cin, cout
  Multiplexer #(.width(32), .disabled(0), .enable("false")) multiplexer_1 (
    .in0(PC), .in1(undriven), .out(multiplexer_1_out), .sel(in_2));
  Register #(.width(32)) u_PC (.D(multiplexer_1_out), .en(in_1), .Q(PC_q), .clk(CK));  // open: clr
  I_MEM i_mem_1 (.ADDRESS(PC_q), .DATA_OUT(i_mem_1_data_out), .CLOCK(CK));
  FBUF fbuf_1 (
    .PC_IN(PC), .INPUT(i_mem_1_data_out), .LOAD(in_3), .CLOCK(CK), .PC_OUT(fbuf_1_pc_out),
    .OPCODE_OUT(fbuf_1_opcode_out), .REG_DST_OUT(fbuf_1_reg_dst_out), .REG_SR1_OUT(fbuf_1_reg_sr1_out),
    .REG_SR2_OUT(fbuf_1_reg_sr2_out), .IMMEDIATE_VAL_OUT(fbuf_1_immediate_val_out));
  Register_File register_file_1 (
    .REG_A(fbuf_1_reg_sr1_out), .REG_B(fbuf_1_reg_sr2_out), .OUT_A(register_file_1_out_a),
    .OUT_B(register_file_1_out_b), .DST_REG(REG_DST), .DATA_IN(DST_VAL), .WE(LD_REG), .CK(CK),
    .ALT_B(fbuf_1_reg_dst_out), .OPCODE_IN(fbuf_1_opcode_out));
  assign bit_extender_1_out = {{16{fbuf_1_immediate_val_out[15]}}, fbuf_1_immediate_val_out};  // Bit_Extender bit_extender_1
  DBUF dbuf_1 (
    .PC_IN(fbuf_1_pc_out), .OPCODE_IN(fbuf_1_opcode_out), .REG_DST_IN(fbuf_1_reg_dst_out),
    .SR1_IN(register_file_1_out_a), .SR2_IN(register_file_1_out_b), .IMM_IN(bit_extender_1_out), .LOAD(in_3),
    .CLOCK(CK), .PC_OUT(dbuf_1_pc_out), .OPCODE_OUT(dbuf_1_opcode_out), .REG_DST_OUT(dbuf_1_reg_dst_out),
    .SR1_OUT(dbuf_1_sr1_out), .SR2_OUT(dbuf_1_sr2_out), .IMM_OUT(dbuf_1_imm_out));
  ALU alu_1 (
    .A_IN(dbuf_1_sr1_out), .B_IN(dbuf_1_sr2_out), .OUT(alu_1_out), .OPCODE(dbuf_1_opcode_out),
    .IMM_IN(dbuf_1_imm_out), .PC_IN(dbuf_1_pc_out), .B_OUT(alu_1_b_out));
  EBUF ebuf_1 (
    .PC_IN(dbuf_1_pc_out), .OPCODE_IN(dbuf_1_opcode_out), .REG_DST_IN(dbuf_1_reg_dst_out),
    .ALU_VAL_IN(alu_1_out), .WORD_VAL_IN(alu_1_b_out), .LOAD(in_3), .CLOCK(CK),
    .OPCODE_OUT(ebuf_1_opcode_out), .REG_DST_OUT(ebuf_1_reg_dst_out), .ALU_VAL_OUT(ebuf_1_alu_val_out),
    .WORD_VAL_OUT(ebuf_1_word_val_out));  // open: PC_OUT
  D_MEM d_mem_1 (
    .ADDRESS(ebuf_1_alu_val_out), .DATA_OUT(d_mem_1_data_out), .DATA_IN(ebuf_1_word_val_out),
    .OPCODE(ebuf_1_opcode_out), .CLOCK(CK));
  Opcode_Dissector opcode_dissector_1 (
    .OPCODE_IN(mbuf_1_opcode_out), .LD_REG(LD_REG));  // open: USE_PC, USE_IMMEDIATE, ALU_SEL, MEM_OP, EXTRA, STORE_WORD
  MBUF mbuf_1 (
    .OPCODE_IN(ebuf_1_opcode_out), .REG_DST_IN(ebuf_1_reg_dst_out), .MEM_VAL_IN(d_mem_1_data_out),
    .LOAD(in_3), .CLOCK(CK), .OPCODE_OUT(mbuf_1_opcode_out), .REG_DST_OUT(REG_DST), .MEM_VAL_OUT(DST_VAL));

  // Other names for the same wires on the sheet: JUMP = in_2; LD = in_3; LD_PC = in_1
endmodule

// F\nBUF
module FBUF (
  input  [31:0] PC_IN,
  input  [31:0] INPUT,
  input  LOAD,
  input  CLOCK,
  output [31:0] PC_OUT,
  output [7:0] OPCODE_OUT,
  output [3:0] REG_DST_OUT,
  output [3:0] REG_SR1_OUT,
  output [3:0] REG_SR2_OUT,
  output [15:0] IMMEDIATE_VAL_OUT
);

  Register #(.width(32)) PC (.D(PC_IN), .en(LOAD), .Q(PC_OUT), .clk(CLOCK));  // open: clr
  Register #(.width(32)) FBUF (
    .D(INPUT), .en(LOAD), .Q({OPCODE_OUT, REG_DST_OUT, REG_SR1_OUT, IMMEDIATE_VAL_OUT}), .clk(CLOCK));  // open: clr

  assign REG_SR2_OUT = IMMEDIATE_VAL_OUT[15:12];
endmodule

// D\nBUF
module DBUF (
  input  [31:0] PC_IN,
  input  [7:0] OPCODE_IN,
  input  [3:0] REG_DST_IN,
  input  [31:0] SR1_IN,
  input  [31:0] SR2_IN,
  input  [31:0] IMM_IN,
  input  LOAD,
  input  CLOCK,
  output [31:0] PC_OUT,
  output [7:0] OPCODE_OUT,
  output [3:0] REG_DST_OUT,
  output [31:0] SR1_OUT,
  output [31:0] SR2_OUT,
  output [31:0] IMM_OUT
);

  Register #(.width(32)) PC (.D(PC_IN), .en(LOAD), .Q(PC_OUT), .clk(CLOCK));  // open: clr
  Register OPCODE (.D(OPCODE_IN), .en(LOAD), .Q(OPCODE_OUT), .clk(CLOCK));  // open: clr
  Register #(.width(4)) REG_DST (.D(REG_DST_IN), .en(LOAD), .Q(REG_DST_OUT), .clk(CLOCK));  // open: clr
  Register #(.width(32)) SR1_VAL (.D(SR1_IN), .en(LOAD), .Q(SR1_OUT), .clk(CLOCK));  // open: clr
  Register #(.width(32)) SR2_VAL (.D(SR2_IN), .en(LOAD), .Q(SR2_OUT), .clk(CLOCK));  // open: clr
  Register #(.width(32)) IMM_VAL (.D(IMM_IN), .en(LOAD), .Q(IMM_OUT), .clk(CLOCK));  // open: clr

  // Other names for the same wires on the sheet: CK = CLOCK; LD = LOAD
endmodule

// E\nBUF
module EBUF (
  input  [31:0] PC_IN,
  input  [7:0] OPCODE_IN,
  input  [3:0] REG_DST_IN,
  input  [31:0] ALU_VAL_IN,
  input  [31:0] WORD_VAL_IN,
  input  LOAD,
  input  CLOCK,
  output [31:0] PC_OUT,
  output [7:0] OPCODE_OUT,
  output [3:0] REG_DST_OUT,
  output [31:0] ALU_VAL_OUT,
  output [31:0] WORD_VAL_OUT
);

  Register #(.width(32)) PC (.D(PC_IN), .en(LOAD), .Q(PC_OUT), .clk(CLOCK));  // open: clr
  Register OPCODE (.D(OPCODE_IN), .en(LOAD), .Q(OPCODE_OUT), .clk(CLOCK));  // open: clr
  Register #(.width(4)) REG_DST (.D(REG_DST_IN), .en(LOAD), .Q(REG_DST_OUT), .clk(CLOCK));  // open: clr
  Register #(.width(32)) ALU_VAL (.D(ALU_VAL_IN), .en(LOAD), .Q(ALU_VAL_OUT), .clk(CLOCK));  // open: clr
  Register #(.width(32)) WORD_VAL (.D(WORD_VAL_IN), .en(LOAD), .Q(WORD_VAL_OUT), .clk(CLOCK));  // open: clr

  // Other names for the same wires on the sheet: CK = CLOCK; LD = LOAD
endmodule

// M\nBUF
module MBUF (
  input  [7:0] OPCODE_IN,
  input  [3:0] REG_DST_IN,
  input  [31:0] MEM_VAL_IN,
  input  LOAD,
  input  CLOCK,
  output [7:0] OPCODE_OUT,
  output [3:0] REG_DST_OUT,
  output [31:0] MEM_VAL_OUT
);

  Register OPCODE (.D(OPCODE_IN), .en(LOAD), .Q(OPCODE_OUT), .clk(CLOCK));  // open: clr
  Register #(.width(4)) REG_DST (.D(REG_DST_IN), .en(LOAD), .Q(REG_DST_OUT), .clk(CLOCK));  // open: clr
  Register #(.width(32)) MEM_VAL (.D(MEM_VAL_IN), .en(LOAD), .Q(MEM_VAL_OUT), .clk(CLOCK));  // open: clr

  // Other names for the same wires on the sheet: CK = CLOCK; LD = LOAD
endmodule

module ALU (
  input  [7:0] OPCODE,
  input  [31:0] PC_IN,
  input  [31:0] A_IN,
  input  [31:0] B_IN,
  input  [31:0] IMM_IN,
  output [31:0] OUT,
  output [31:0] B_OUT
);

  wire USE_IMM, USE_PC;
  wire [1:0] opcode_dissector_1_alu_sel;
  wire [31:0] A, adder_1_out, and_1_out, B, not_1_out, subtractor_1_out;

  Multiplexer #(.width(32), .disabled(0), .enable("false")) multiplexer_1 (
    .in0(A_IN), .in1(PC_IN), .out(A), .sel(USE_PC));
  Multiplexer #(.width(32), .disabled(0), .enable("false")) multiplexer_2 (
    .in0(B_IN), .in1(IMM_IN), .out(B), .sel(USE_IMM));
  Opcode_Dissector opcode_dissector_1 (
    .USE_PC(USE_PC), .USE_IMMEDIATE(USE_IMM), .ALU_SEL(opcode_dissector_1_alu_sel), .OPCODE_IN(OPCODE));  // open: MEM_OP, LD_REG, EXTRA, STORE_WORD
  Adder #(.width(32)) adder_1 (.a(A), .b(B), .out(adder_1_out));  // open: cin, cout
  assign and_1_out = A & B;  // AND_Gate and_1, 32 bits wide
  assign not_1_out = ~and_1_out;  // NOT_Gate not_1, 32 bits wide
  Subtractor #(.width(32)) subtractor_1 (.a(A), .b(B), .out(subtractor_1_out));  // open: bin, bout
  Multiplexer #(.select(2), .width(32), .disabled(0), .enable("false")) multiplexer_3 (
    .in0(adder_1_out), .in1(not_1_out), .in2(subtractor_1_out), .in3(A), .out(OUT),
    .sel(opcode_dissector_1_alu_sel));

  assign B_OUT = B_IN;
endmodule

// REG \nFILE
module Register_File (
  input  [7:0] OPCODE_IN,
  input  [3:0] DST_REG,
  input  [31:0] DATA_IN,
  input  [3:0] REG_A,
  input  [3:0] REG_B,
  input  [3:0] ALT_B,
  input  CK,
  input  WE,
  output [31:0] OUT_A,
  output [31:0] OUT_B
);

  wire A_0, B_0, demultiplexer_1_out0, demultiplexer_1_out1, demultiplexer_1_out2, demultiplexer_1_out3,
       USE_ALT;
  wire [1:0] B_GRP, B_REG;
  wire [31:0] multiplexer_2_out, multiplexer_5_out, register_group_1_out_a, register_group_1_out_b,
       register_group_2_out_a, register_group_2_out_b, register_group_3_out_a, register_group_3_out_b,
       register_group_4_out_a, register_group_4_out_b;

  Multiplexer #(.width(4), .disabled(0), .enable("false")) multiplexer_1 (
    .in0(REG_B), .in1(ALT_B), .out({B_GRP, B_REG}), .sel(USE_ALT));
  Opcode_Dissector opcode_dissector_1 (
    .OPCODE_IN(OPCODE_IN), .STORE_WORD(USE_ALT));  // open: USE_PC, USE_IMMEDIATE, ALU_SEL, MEM_OP, LD_REG, EXTRA
  Comparator #(.width(4), .mode("unsigned")) comparator_1 (.a(4'b0000), .b(REG_A), .eq(A_0));  // open: gt, lt
  Comparator #(.width(4), .mode("unsigned")) comparator_2 (.a({B_GRP, B_REG}), .b(4'b0000), .eq(B_0));  // open: gt, lt
  Demultiplexer #(.select(2), .disabled(0), .enable("false")) demultiplexer_1 (
    .out0(demultiplexer_1_out0), .out1(demultiplexer_1_out1), .out2(demultiplexer_1_out2),
    .out3(demultiplexer_1_out3), .in(WE), .sel(DST_REG[3:2]));
  Register_Group register_group_1 (
    .REG_A(REG_A[1:0]), .REG_B(B_REG), .DATA_IN(DATA_IN), .DST_REG(DST_REG[1:0]), .WE(demultiplexer_1_out0),
    .CK(CK), .OUT_A(register_group_1_out_a), .OUT_B(register_group_1_out_b));
  Register_Group register_group_2 (
    .REG_A(REG_A[1:0]), .REG_B(B_REG), .DATA_IN(DATA_IN), .DST_REG(DST_REG[1:0]), .WE(demultiplexer_1_out1),
    .CK(CK), .OUT_A(register_group_2_out_a), .OUT_B(register_group_2_out_b));
  Register_Group register_group_3 (
    .REG_A(REG_A[1:0]), .REG_B(B_REG), .DATA_IN(DATA_IN), .DST_REG(DST_REG[1:0]), .WE(demultiplexer_1_out2),
    .CK(CK), .OUT_A(register_group_3_out_a), .OUT_B(register_group_3_out_b));
  Register_Group register_group_4 (
    .REG_A(REG_A[1:0]), .REG_B(B_REG), .DATA_IN(DATA_IN), .DST_REG(DST_REG[1:0]), .WE(demultiplexer_1_out3),
    .CK(CK), .OUT_A(register_group_4_out_a), .OUT_B(register_group_4_out_b));
  Multiplexer #(.select(2), .width(32), .disabled(0), .enable("false")) multiplexer_2 (
    .in0(register_group_1_out_a), .in1(register_group_2_out_a), .in2(register_group_3_out_a),
    .in3(register_group_4_out_a), .out(multiplexer_2_out), .sel(REG_A[3:2]));
  Multiplexer #(.width(32), .disabled(0), .enable("false")) multiplexer_3 (
    .in0(multiplexer_2_out), .in1({32{1'b0}}), .out(OUT_A), .sel(A_0));
  Multiplexer #(.width(32), .disabled(0), .enable("false")) multiplexer_4 (
    .in0(multiplexer_5_out), .in1({32{1'b0}}), .out(OUT_B), .sel(B_0));
  Multiplexer #(.select(2), .width(32), .disabled(0), .enable("false")) multiplexer_5 (
    .in0(register_group_1_out_b), .in1(register_group_2_out_b), .in2(register_group_3_out_b),
    .in3(register_group_4_out_b), .out(multiplexer_5_out), .sel(B_GRP));

  // Other names for the same wires on the sheet: D_REG[1:0] = DST_REG[1:0]; D_GRP[1:0] = DST_REG[3:2];
  //   A_REG[1:0] = REG_A[1:0]; A_GRP[1:0] = REG_A[3:2]
endmodule

module Register_Group (
  input  [31:0] DATA_IN,
  input  [1:0] DST_REG,
  input  [1:0] REG_A,
  input  [1:0] REG_B,
  input  WE,
  input  CK,
  output [31:0] OUT_A,
  output [31:0] OUT_B
);

  wire demultiplexer_1_out0, demultiplexer_1_out1, demultiplexer_1_out2, demultiplexer_1_out3;
  wire [31:0] register_1_q, register_2_q, register_3_q, register_4_q;

  Demultiplexer #(.select(2), .disabled(0), .enable("false")) demultiplexer_1 (
    .out0(demultiplexer_1_out0), .out1(demultiplexer_1_out1), .out2(demultiplexer_1_out2),
    .out3(demultiplexer_1_out3), .in(WE), .sel(DST_REG));
  Register #(.width(32)) register_1 (.D(DATA_IN), .en(demultiplexer_1_out0), .Q(register_1_q), .clk(CK));  // open: clr
  Register #(.width(32)) register_2 (.D(DATA_IN), .en(demultiplexer_1_out1), .Q(register_2_q), .clk(CK));  // open: clr
  Register #(.width(32)) register_3 (.D(DATA_IN), .en(demultiplexer_1_out2), .Q(register_3_q), .clk(CK));  // open: clr
  Register #(.width(32)) register_4 (.D(DATA_IN), .en(demultiplexer_1_out3), .Q(register_4_q), .clk(CK));  // open: clr
  Multiplexer #(.select(2), .width(32), .disabled(0), .enable("false")) multiplexer_1 (
    .in0(register_1_q), .in1(register_2_q), .in2(register_3_q), .in3(register_4_q), .out(OUT_A), .sel(REG_A));
  Multiplexer #(.select(2), .width(32), .disabled(0), .enable("false")) multiplexer_2 (
    .in0(register_1_q), .in1(register_2_q), .in2(register_3_q), .in3(register_4_q), .out(OUT_B), .sel(REG_B));
endmodule

// I\nMEM
module I_MEM (
  input  [31:0] ADDRESS,
  input  CLOCK,
  output [31:0] DATA_OUT
);

  wire not_1_out;

  not not_1 (not_1_out, 1'b0);
  RAM #(.addrWidth(24), .dataWidth(32), .bus("separate")) ram_1 (
    .addr(ADDRESS[23:0]), .din({32{1'b0}}), .data(DATA_OUT), .str(1'b0), .clk(CLOCK), .ld(not_1_out));  // open: sel, clr

  // Other names for the same wires on the sheet: TRASH[7:0] = ADDRESS[31:24]
endmodule

// DISSECT
module Opcode_Dissector (
  input  [7:0] OPCODE_IN,
  output STORE_WORD,
  output USE_PC,
  output USE_IMMEDIATE,
  output [1:0] ALU_SEL,
  output [1:0] MEM_OP,
  output LD_REG,
  output EXTRA
);

  Decoder #(.select(2), .enable("false")) decoder_1 (
    .out2(STORE_WORD), .sel(OPCODE_IN[3:2]));  // open: out0, out1, out3

  assign ALU_SEL = OPCODE_IN[5:4];
  assign EXTRA = OPCODE_IN[0];
  assign LD_REG = OPCODE_IN[1];
  assign MEM_OP = OPCODE_IN[3:2];
  assign USE_IMMEDIATE = OPCODE_IN[6];
  assign USE_PC = OPCODE_IN[7];
endmodule

// D\nMEM
module D_MEM (
  input  [7:0] OPCODE,
  input  [31:0] DATA_IN,
  input  [31:0] ADDRESS,
  input  CLOCK,
  output [31:0] DATA_OUT
);

  wire STORE;
  wire [1:0] opcode_dissector_1_mem_op;
  wire [31:0] ram_1_data;

  RAM #(.addrWidth(24), .dataWidth(32), .bus("separate")) ram_1 (
    .addr(ADDRESS[23:0]), .din(DATA_IN), .data(ram_1_data), .str(STORE), .clk(CLOCK));  // open: sel, ld, clr
  Opcode_Dissector opcode_dissector_1 (
    .MEM_OP(opcode_dissector_1_mem_op), .OPCODE_IN(OPCODE), .STORE_WORD(STORE));  // open: USE_PC, USE_IMMEDIATE, ALU_SEL, LD_REG, EXTRA
  Multiplexer #(.select(2), .width(32), .disabled(0), .enable("false")) multiplexer_1 (
    .in0(ADDRESS), .in1(ram_1_data), .out(DATA_OUT), .sel(opcode_dissector_1_mem_op));  // open: in2, in3

  // Other names for the same wires on the sheet: PASS[31:0] = ADDRESS; TRASH[7:0] = ADDRESS[31:24]
endmodule
